# Fritzing sketch CarLightcontrol (saved by Fritzing 0.9.10b)
perfboards: 2

parts:
  J1 = JST XH 2A male [form="♂ (male)" package=THT]  # not connected
  U1 = JST-XH-6A  # not connected
  Q1 = TRANSISTOR_NPN [package=to-92-ammo]
  Ruecklicht_(35) = JST XH 3A Male [chip_label=? package=THT]  # not connected
  Rueckfahr_(34) = JST XH 3A Male [chip_label=? package=THT]  # not connected
  Brems_(39) = JST XH 3A Male [chip_label=? package=THT]  # not connected
  Blink_(36) = JST XH 3A Male [chip_label=? package=THT]  # not connected
  J2 = rounded female pin header, 15 pins [form="♀ (female rounded)"]  # not connected
  J3 = rounded female pin header, 15 pins [form="♀ (female rounded)"]  # not connected
  R4 = Resistor upright [tolerance=±5% resistance=2200 package=THT]  # not connected
  Q2 = TRANSISTOR_NPN [package=to-92-ammo]
  R6 = Resistor upright [tolerance=±5% resistance=2200 package=THT]  # not connected
  Q3 = TRANSISTOR_NPN [package=to-92-ammo]
  R8 = Resistor upright [tolerance=±5% resistance=2200 package=THT]  # not connected
  R10 = Resistor upright [tolerance=±5% resistance=2200 package=THT]  # not connected
  R11 = Resistor upright [tolerance=±5% resistance=2200 package=THT]
  R12 = Resistor upright [tolerance=±5% resistance=2200 package=THT]
  R13 = Resistor upright [tolerance=±5% resistance=2200 package=THT]
  R14 = Resistor upright [tolerance=±5% resistance=2200 package=THT]
  J4 = rounded female pin header, 3 pins [form="♀ (female rounded)"]  # not connected
  J5 = rounded female pin header, 3 pins [form="♀ (female rounded)"]  # not connected
  J6 = rounded female pin header, 3 pins [form="♀ (female rounded)"]  # not connected
  J7 = rounded female pin header, 3 pins [form="♀ (female rounded)"]  # not connected
  J8 = rounded female pin header, 3 pins [form="♀ (female rounded)"]
  J9 = rounded female pin header, 3 pins [form="♀ (female rounded)"]
  J10 = rounded female pin header, 3 pins [form="♀ (female rounded)"]
  J12 = rounded female pin header, 1 pin [form="♀ (female rounded)"]  # not connected
  J13 = rounded female pin header, 1 pin [form="♀ (female rounded)"]  # not connected
  J14 = rounded female pin header, 1 pin [form="♀ (female rounded)"]  # not connected
  J15 = rounded female pin header, 1 pin [form="♀ (female rounded)"]  # not connected
  J16 = rounded female pin header, 1 pin [form="♀ (female rounded)"]
  J17 = rounded female pin header, 1 pin [form="♀ (female rounded)"]
  J18 = rounded female pin header, 1 pin [form="♀ (female rounded)"]
  J19 = rounded female pin header, 1 pin [form="♀ (female rounded)"]
  J20 = rounded female pin header, 2 pins [form="♀ (female rounded)"]
  J21 = rounded female pin header, 6 pins [form="♀ (female rounded)"]
  J22 = rounded female pin header, 15 pins [form="♀ (female rounded)"]
  J23 = rounded female pin header, 15 pins [form="♀ (female rounded)"]
  J24 = rounded female pin header, 3 pins [form="♀ (female rounded)"]
  J25 = rounded female pin header, 3 pins [form="♀ (female rounded)"]
  J26 = rounded female pin header, 3 pins [form="♀ (female rounded)"]
  J27 = rounded female pin header, 3 pins [form="♀ (female rounded)"]
  J28 = rounded female pin header, 2 pins [form="♀ (female rounded)"]
  J29 = rounded female pin header, 2 pins [form="♀ (female rounded)"]  # not connected
  J31 = rounded female pin header, 2 pins [form="♀ (female rounded)"]  # not connected
  J32 = rounded female pin header, 2 pins [form="♀ (female rounded)"]
  MP1584EN_Board1 = MP1584EN Power Regulator Board [part_number=MP1584EN]  # not connected
  Q4 = TRANSISTOR_NPN_2 [package=to-92]
  Ruecklicht_(13) = Basic FET P-Channel [package="DPak [SMD]"]  # not connected
  Rueckfahr_(27) = Basic FET P-Channel [package="DPak [SMD]"]  # not connected
  Brems_(33) = Basic FET P-Channel [package="DPak [SMD]"]  # not connected
  Blink_(32) = Basic FET P-Channel [package="DPak [SMD]"]  # not connected
  J11 = rounded female pin header, 3 pins [form="♀ (female rounded)"]

nets:
  N1: Q1.B, R11.Pin_1
  N2: Q2.B, R12.Pin_1
  N3: Q3.B, R13.Pin_1
  N4: R14.Pin_1, Q4.B
  N5: J8.pin2, J21.pin1
  N6: J9.pin2, J21.pin2
  N7: J10.pin2, J21.pin4
  N8: J16.pin1, J22.pin6
  N9: J17.pin1, J22.pin7
  N10: J18.pin1, J22.pin10
  N11: J19.pin1, J22.pin13
  N12: J20.pin1, J28.pin2
  N13: J21.pin5, J11.pin2
  N14: J22.pin2, J24.pin1
  N15: J22.pin3, J25.pin1
  N16: J22.pin4, J26.pin1
  N17: J22.pin5, J27.pin1
  N18: J22.pin15, J32.pin1
  N19: J23.pin15, J27.pin3

notes:
  Yellow: 12 V
  Black: Gnd
  Red: 5 V
  Orange: 3.3 V
  Green: AnalogIn (Max 3.3 V)
  NPN: BC237
  FET-P: IRF9540N

custom parts:
  JST XH 2A male: JST XH-2A
  JST-XH-6A: JST XH 6A (2.54)
  JST XH 3A Male: 2.54 Mm JST "XH" connector
  Resistor upright: A generic upright standing resistor (0.25W)
  MP1584EN Power Regulator Board: The MP1584EN is a high frequency step-down switching regulator. The input voltage range is 4.5V to 28V. The output voltage is set by the board's potentiometer.
